// Logisim project Main bus.circ as structural Verilog: 1 circuit, main circuit Main bus
module Main_bus (
  input  in_1,
  input  in_2
);

  wire undriven, undriven_2, undriven_3, undriven_4, undriven_5, undriven_6, undriven_7, undriven_8;
  wire [6:0] keyboard_1_data;
  wire [15:0] Accumulator_register_q, controlled_buffer_1_out, controlled_buffer_3_out,
       controlled_buffer_4_out, controlled_buffer_5_out, controlled_buffer_7_out, Input_register_2_q,
       Input_register_q, Instruction_register_q, Memory_access_register_q, Program_counter_q, ram_1_data,
       rom_1_data, undriven_9;

  Counter #(.width(16), .max('hffff)) Program_counter (.Q(Program_counter_q));  // open: load, D, count, carry, clk, clr
  Register #(.width(16)) Memory_access_register (
    .D(controlled_buffer_3_out), .Q(Memory_access_register_q));  // open: en, clk, clr
  Register #(.width(16)) Instruction_register (
    .D(controlled_buffer_7_out), .Q(Instruction_register_q));  // open: en, clk, clr
  RAM #(.addrWidth(16), .dataWidth(16)) ram_1 (
    .addr(Memory_access_register_q), .data(ram_1_data), .ld(undriven_2));  // open: sel, clk, clr
  ROM #(.addrWidth(16), .dataWidth(16)) rom_1 (.addr(Instruction_register_q), .data(rom_1_data));  // open: sel
  assign controlled_buffer_1_out = undriven_6 ? Accumulator_register_q : 16'bz;  // Controlled_Buffer controlled_buffer_1
  assign controlled_buffer_1_out = undriven ? Program_counter_q : 16'bz;  // Controlled_Buffer controlled_buffer_2
  assign controlled_buffer_3_out = undriven_2 ? controlled_buffer_1_out : 16'bz;  // Controlled_Buffer controlled_buffer_3
  assign controlled_buffer_4_out = undriven_7 ? controlled_buffer_1_out : 16'bz;  // Controlled_Buffer controlled_buffer_4
  assign controlled_buffer_5_out = undriven_8 ? controlled_buffer_1_out : 16'bz;  // Controlled_Buffer controlled_buffer_5
  assign controlled_buffer_1_out = undriven_4 ? ram_1_data : 16'bz;  // Controlled_Buffer controlled_buffer_6
  assign controlled_buffer_7_out = undriven_3 ? controlled_buffer_1_out : 16'bz;  // Controlled_Buffer controlled_buffer_7
  assign controlled_buffer_1_out = undriven_5 ? rom_1_data : 16'bz;  // Controlled_Buffer controlled_buffer_8
  Keyboard keyboard_1 (.clk(in_1), .clr(in_2), .data(keyboard_1_data));  // open: re, avail
  TTY tty_1 (.data(keyboard_1_data), .clk(in_1), .clr(in_2));  // open: we
  Register #(.width(16)) Accumulator_register (.D(undriven_9), .Q(Accumulator_register_q));  // open: en, clk, clr
  Register #(.width(16)) Input_register (.D(controlled_buffer_4_out), .Q(Input_register_q));  // open: en, clk, clr
  Register #(.width(16)) Input_register_2 (.D(controlled_buffer_5_out), .Q(Input_register_2_q));  // open: en, clk, clr
  Register #(.width(16)) Output_register ();  // open: D, en, Q, clk, clr

  // Notes on the sheet:
  //   ROM for control matrix
  //   ALU
endmodule
